# Fritzing sketch exercicio-01 (saved by Fritzing 1.0.4)

parts:
  Componente1 = Arduino Uno (Rev3)
  LED2 = smd LED [color="Red (633nm)" package="0805 [SMD]"]

nets:
  N1: Componente1.D13/SCK, LED2.anode
  N2: Componente1.GND, LED2.cathode

// code stored in the sketch: exercicio-02.fzz.ino
void setup()
{
  pinMode(13, OUTPUT); // Define que vamos utilizar o pino 13 no modo de saída
}

void loop()
{
  digitalWrite(13, LOW);		// Manda um pulso baixo (desligado) no pino 13
  delay(1000); 					 		// Aguarda 1 segundo
  digitalWrite(13, HIGH);		// Manda um pulso alto (ligado) no pino 13
  delay(1000); 							// Aguarda 1 segundo
}
