# Fritzing sketch exercicio-03 (saved by Fritzing 1.0.4)
breadboards: 1

parts:
  Componente1 = Arduino Uno (Rev3)
  LED2 = smd LED [color="Red (633nm)" package="0805 [SMD]"]
  LED3 = LED - 5mm [color="Yellow (595nm)" current=0.030A package="5 mm [THT]"]
  LED4 = LED - 5mm [color="Green (555nm)" current=0.030A package="5 mm [THT]"]
  R1 = Resistor [tolerance=±5% power=0.25W resistance=1k package=THT]
  R2 = Resistor [tolerance=±5% power=0.25W resistance=1k package=THT]
  R3 = Resistor [tolerance=±5% power=0.25W resistance=1k package=THT]

nets:
  N1: Componente1.D11_PWM/MOSI, R3.Pin_0
  N2: Componente1.D12/MISO, R2.Pin_0
  N3: Componente1.D13/SCK, R1.Pin_0
  N4: Componente1.GND, LED2.cathode, LED3.cathode, LED4.cathode
  N5: LED2.anode, R1.Pin_1
  N6: LED3.anode, R2.Pin_1
  N7: LED4.anode, R3.Pin_1
