# Fritzing sketch exercicio-01 (saved by Fritzing 1.0.4)
breadboards: 1

parts:
  Componente1 = Arduino Uno (Rev3)
  S1 = Pushbutton [package="[SMD]"]
  R1 = Resistor [tolerance=±5% power=0.25W resistance=1k package=THT]
  LED1 = LED - 5mm [color="Red (633nm)" current=0.030A package="5 mm [THT]"]
  R2 = Resistor [tolerance=±5% power=0.25W resistance=1k package=THT]

nets:
  N1: Componente1.D13/SCK, R2.Pin_1
  N2: Componente1.D2, S1.Pin_1, S1.Pin_2, R1.Pin_0
  N3: Componente1.5V, S1.Pin_3, S1.Pin_4
  N4: Componente1.GND, R1.Pin_1, LED1.cathode
  N5: LED1.anode, R2.Pin_0
