# Fritzing sketch exercicio-02 (saved by Fritzing 1.0.4)
breadboards: 1

parts:
  Componente1 = Arduino Uno (Rev3)
  S1 = Pushbutton [package="[SMD]"]
  R1 = Resistor [tolerance=±5% power=0.25W resistance=1k package=THT]
  LED1 = LED - 5mm [color="Red (633nm)" current=0.030A package="5 mm [THT]"]
  R2 = Resistor [tolerance=±5% power=0.25W resistance=1k package=THT]
  LED2 = LED - 5mm [color="Red (633nm)" current=0.030A package="5 mm [THT]"]
  R3 = Resistor [tolerance=±5% power=0.25W resistance=1k package=THT]

nets:
  N1: Componente1.D12/MISO, R3.Pin_1
  N2: Componente1.D13/SCK, R2.Pin_1
  N3: Componente1.D2, S1.Pin_1, S1.Pin_2, R1.Pin_0
  N4: Componente1.5V, S1.Pin_3, S1.Pin_4
  N5: Componente1.GND, R1.Pin_1, LED1.cathode, LED2.cathode
  N6: LED1.anode, R2.Pin_0
  N7: LED2.anode, R3.Pin_0
