# Fritzing sketch exercicio-03 (saved by Fritzing 1.0.4)
breadboards: 1

parts:
  Componente1 = Arduino Uno (Rev3)
  S1 = Pushbutton [package="[SMD]"]
  R1 = Resistor [tolerance=±5% power=0.25W resistance=1k package=THT]
  LED1 = LED - 5mm [color="Red (633nm)" current=0.030A package="5 mm [THT]"]
  R2 = Resistor [tolerance=±5% power=0.25W resistance=1k package=THT]
  LED2 = LED - 5mm [color="Red (633nm)" current=0.030A package="5 mm [THT]"]
  R3 = Resistor [tolerance=±5% power=0.25W resistance=1k package=THT]
  LED3 = LED - 5mm [color="Red (633nm)" current=0.030A package="5 mm [THT]"]
  R4 = Resistor [tolerance=±5% power=0.25W resistance=1k package=THT]
  LED4 = LED - 5mm [color="Red (633nm)" current=0.030A package="5 mm [THT]"]
  R5 = Resistor [tolerance=±5% power=0.25W resistance=1k package=THT]

nets:
  N1: Componente1.D10_PWM/SS, R5.Pin_0
  N2: Componente1.D11_PWM/MOSI, R4.Pin_0
  N3: Componente1.D12/MISO, R3.Pin_0
  N4: Componente1.D13/SCK, R2.Pin_0
  N5: Componente1.D2, S1.Pin_1, S1.Pin_2, R1.Pin_0
  N6: Componente1.5V, S1.Pin_3, S1.Pin_4
  N7: Componente1.GND, R1.Pin_1, LED1.cathode, LED2.cathode, LED3.cathode, LED4.cathode
  N8: LED1.anode, R2.Pin_1
  N9: LED2.anode, R3.Pin_1
  N10: LED3.anode, R4.Pin_1
  N11: LED4.anode, R5.Pin_1
