# Fritzing sketch exercicio-01 (saved by Fritzing 1.0.4)
breadboards: 1

parts:
  R1 = Rotary Potentiometer (Large) [maximum_resistance=100kΩ knob_status=50% power=0.5W package=THT]
  Componente1 = Arduino Uno (Rev3)

nets:
  N1: R1.leg1, Componente1.GND
  N2: R1.wiper, Componente1.A0
  N3: R1.leg2, Componente1.5V
