# Fritzing sketch exercicio-03 (saved by Fritzing 1.0.4)
breadboards: 1

parts:
  R1 = Rotary Potentiometer (Large) [maximum_resistance=100kΩ knob_status=50% power=0.5W package=THT]
  Componente1 = Arduino Uno (Rev3)
  LED1 = smd LED [color="Red (633nm)" package="0805 [SMD]"]
  S1 = Pushbutton [package="[SMD]"]
  R2 = Resistor [tolerance=±5% resistance=220 package="2010 [SMD]"]

nets:
  N1: R1.leg1, Componente1.GND, LED1.cathode, R2.Pin_1
  N2: R1.wiper, Componente1.A0
  N3: R1.leg2, Componente1.5V, S1.Pin_3, S1.Pin_4
  N4: Componente1.D13/SCK, LED1.anode
  N5: Componente1.D7, S1.Pin_1, S1.Pin_2, R2.Pin_0
