# Fritzing sketch exercicio-01 (saved by Fritzing 1.0.4)
breadboards: 1

parts:
  Componente1 = Arduino Uno (Rev3)
  HC-SR04_Sensor_1 = HC-SR04 Ultrasonic Distance Sensor
  LED1 = smd LED [color="Red (633nm)" package="0805 [SMD]"]

nets:
  N1: Componente1.D13/SCK, LED1.anode
  GND: Componente1.GND, HC-SR04_Sensor_1.GND, LED1.cathode
  N2: Componente1.D5_PWM, HC-SR04_Sensor_1.ECHO
  N3: Componente1.D6_PWM, HC-SR04_Sensor_1.TRIG
  5V: Componente1.5V, HC-SR04_Sensor_1.VCC
