# Fritzing sketch exercicio-02 (saved by Fritzing 1.0.4)
breadboards: 1

parts:
  Componente1 = Arduino Uno (Rev3)
  HC-SR04_Sensor_1 = HC-SR04 Ultrasonic Distance Sensor
  LED1 = smd LED [color="Red (633nm)" package="0805 [SMD]"]
  R1 = Rotary Potentiometer (Large) [maximum_resistance=10kΩ knob_status=50% power=0.5W package=THT]

nets:
  N1: Componente1.A0, R1.wiper
  N2: Componente1.D13/SCK, LED1.anode
  GND: Componente1.GND, HC-SR04_Sensor_1.GND, LED1.cathode, R1.leg1
  N3: Componente1.D5_PWM, HC-SR04_Sensor_1.ECHO
  N4: Componente1.D6_PWM, HC-SR04_Sensor_1.TRIG
  5V: Componente1.5V, HC-SR04_Sensor_1.VCC, R1.leg2
