# Fritzing sketch exercicio-03 (saved by Fritzing 1.0.4)
breadboards: 1

parts:
  Mod1 = KY-015 Temperature & Humidity Sensor Module [package="Breakout board"]
  LED1 = smd LED [color="Red (633nm)" package="0805 [SMD]"]
  LED2 = smd LED [color="Yellow (595nm)" package="0805 [SMD]"]
  LED3 = smd LED [color="Green (570nm)" package="0805 [SMD]"]
  Componente1 = Arduino Uno (Rev3)

nets:
  N1: Mod1.S, Componente1.D2
  VIN: Mod1.Vin, Mod1.-, Componente1.5V
  N2: LED1.cathode, LED2.cathode, LED3.cathode, Componente1.GND
  N3: LED1.anode, Componente1.D7
  N4: LED2.anode, Componente1.D8
  N5: LED3.anode, Componente1.D9_PWM

custom parts:
  KY-015 Temperature & Humidity Sensor Module: KY-015 temperature and humidity sensor module, provides a low-latency serial interface to measure humidity and temperature.
