# Fritzing sketch configuração HC-05 (saved by Fritzing 1.0.4)
breadboards: 1

parts:
  Componente1 = Arduino Uno (Rev3) - ICSP
  Componente2 = Bluetooth HC-05 Macho
  R1 = Resistor [tolerance=±5% resistance=1k power=0.25W package=THT]
  R2 = Resistor [tolerance=±5% resistance=2.2k power=0.25W package=THT]

nets:
  N1: Componente1.D0/RX, R1.Pin_1
  N2: Componente1.D1/TX, Componente2.TXD
  5V: Componente1.5V, Componente2.VCC, Componente2.Key
  GND: Componente1.GND, Componente2.GND, R2.Pin_0
  N3: Componente2.RXD, R1.Pin_0, R2.Pin_1
