# Fritzing sketch exercicio-02 (saved by Fritzing 1.0.4)
breadboards: 1

parts:
  Componente1 = Arduino Uno (Rev3) - ICSP
  Componente2 = Bluetooth HC-05 Macho
  R1 = Resistor [tolerance=±5% resistance=1k power=0.25W package=THT]
  R2 = Resistor [tolerance=±5% resistance=2.2k power=0.25W package=THT]
  LED1 = LED - 3mm [color="Red (633nm)" current=0.030A package="3 mm [THT]"]
  R3 = Resistor [tolerance=±5% resistance=1k power=0.25W package=THT]

nets:
  N1: Componente1.D13/SCK, R3.Pin_0
  N2: Componente1.D0/RX, Componente2.TXD
  N3: Componente1.D1/TX, R1.Pin_1
  5V: Componente1.5V, Componente2.VCC
  GND: Componente1.GND, Componente2.GND, R2.Pin_0, LED1.cathode
  N4: Componente2.RXD, R1.Pin_0, R2.Pin_1
  N5: LED1.anode, R3.Pin_1
