# Fritzing sketch exercicio-03 (saved by Fritzing 1.0.4)
breadboards: 1

parts:
  Componente1 = Arduino Uno (Rev3) - ICSP
  Componente2 = Bluetooth HC-05 Macho
  R1 = Resistor [tolerance=±5% resistance=1k power=0.25W package=THT]
  R2 = Resistor [tolerance=±5% resistance=2.2k power=0.25W package=THT]
  S1 = Pushbutton [package="[THT]"]
  LED1 = LED - 5mm [color="Red (633nm)" current=0.030A package="5 mm [THT]"]
  R3 = Resistor [tolerance=±5% resistance=1k power=0.25W package=THT]

nets:
  N1: Componente1.ICSP_SCK, Componente1.D13/SCK, S1.Pin_1, S1.Pin_2
  N2: Componente1.D10_PWM/SS, Componente2.TXD
  N3: Componente1.D11_PWM/MOSI, R1.Pin_1
  N4: Componente1.D5_PWM, R3.Pin_0
  5V: Componente1.5V, Componente2.VCC, S1.Pin_3, S1.Pin_4
  GND: Componente1.GND, Componente2.GND, R2.Pin_0, LED1.cathode
  N5: Componente2.RXD, R1.Pin_0, R2.Pin_1
  N6: LED1.anode, R3.Pin_1
