# Fritzing sketch exercicio-02 (saved by Fritzing 1.0.4)
circuit board: 5.95923cm x 6.3306cm
breadboards: 1

parts:
  Arduino_UNO = Arduino Uno (Rev3)
  Relay_5V = Keyes Relay [package=THT]
  R1 = Rotary Potentiometer (Small) [maximum_resistance=10kΩ knob_status=50% power=0.5W package=THT]
  LED1 = LED - 5mm [color="Red (633nm)" current=0.030A package="5 mm [THT]"]

nets:
  N1: Arduino_UNO.A0, R1.wiper
  N2: Arduino_UNO.D9_PWM, LED1.anode
  N3: Arduino_UNO.D13/SCK, Relay_5V.signal
  N4: Arduino_UNO.GND, Relay_5V.ground, R1.leg1, LED1.cathode
  N5: Arduino_UNO.5V, Relay_5V.power, R1.leg2
  N6: Relay_5V.NC, Relay_5V.C, Relay_5V.NO

custom parts:
  Keyes Relay: The Keyes 5V relay module is suitable for SCM development, home appliance control. It uses a 5V~12V TIL control signal which can control DC / AC signal.

// code stored in the sketch: bluetoothLight.ino
char blueToothVal;           //value sent over via bluetooth
char lastValue;              //stores last state of device (on/off)
 
void setup()
{
 Serial.begin(9600); 
 pinMode(13,OUTPUT);
 pinMode(12,INPUT);
}
 
 
void loop()
{
  if(Serial.available())
  {//if there is data being recieved
    blueToothVal=Serial.read(); //read it
  }
  if (blueToothVal=='n')
  {//if value from bluetooth serial is n
    digitalWrite(13,HIGH);            //switch on LED
    if (lastValue!='n')
      Serial.println(F("LED is on")); //print LED is on
    lastValue=blueToothVal;
  }
  else if (blueToothVal=='f')
  {//if value from bluetooth serial is n
    digitalWrite(13,LOW);             //turn off LED
    if (lastValue!='f')
      Serial.println(F("LED is off")); //print LED is on
    lastValue=blueToothVal;
  }
  delay(250);
}
