# Fritzing sketch exercicio-03 (saved by Fritzing 1.0.4)
circuit board: 5.95923cm x 6.3306cm
breadboards: 1

parts:
  Arduino_UNO = Arduino Uno (Rev3)
  Relay_5V = Keyes Relay [package=THT]
  Mod1 = KY-015 Temperature & Humidity Sensor Module [package="Breakout board"]
  LED2 = RGB LED (com. cathode, rgb) [color="Red (633nm)" current=0.030A package="5 mm [THT]"]

nets:
  N1: Arduino_UNO.D9_PWM, LED2.red_anode
  N2: Arduino_UNO.D10_PWM/SS, LED2.green_anode
  N3: Arduino_UNO.D11_PWM/MOSI, LED2.blue_anode
  N4: Arduino_UNO.D13/SCK, Relay_5V.signal
  N5: Arduino_UNO.GND, Relay_5V.ground, Mod1.-, LED2.common_cathode
  N6: Arduino_UNO.D2, Mod1.S
  5V: Arduino_UNO.5V, Relay_5V.power, Mod1.Vin
  N7: Relay_5V.NC, Relay_5V.C, Relay_5V.NO

custom parts:
  Keyes Relay: The Keyes 5V relay module is suitable for SCM development, home appliance control. It uses a 5V~12V TIL control signal which can control DC / AC signal.
  KY-015 Temperature & Humidity Sensor Module: KY-015 temperature and humidity sensor module, provides a low-latency serial interface to measure humidity and temperature.

// code stored in the sketch: bluetoothLight.ino
char blueToothVal;           //value sent over via bluetooth
char lastValue;              //stores last state of device (on/off)
 
void setup()
{
 Serial.begin(9600); 
 pinMode(13,OUTPUT);
 pinMode(12,INPUT);
}
 
 
void loop()
{
  if(Serial.available())
  {//if there is data being recieved
    blueToothVal=Serial.read(); //read it
  }
  if (blueToothVal=='n')
  {//if value from bluetooth serial is n
    digitalWrite(13,HIGH);            //switch on LED
    if (lastValue!='n')
      Serial.println(F("LED is on")); //print LED is on
    lastValue=blueToothVal;
  }
  else if (blueToothVal=='f')
  {//if value from bluetooth serial is n
    digitalWrite(13,LOW);             //turn off LED
    if (lastValue!='f')
      Serial.println(F("LED is off")); //print LED is on
    lastValue=blueToothVal;
  }
  delay(250);
}
